// Logisim project CPU.circ as structural Verilog: 5 circuits, main circuit MAIN
module MAIN (
  input  in_1,
  input  RST
);

  wire and_1_out, and_2_out, and_3_out, and_4_out, and_5_out, and_6_out, and_7_out, and_8_out, and_9_out,
       and_10_out, com_clk_1_clk, or_1_out, or_2_out, or_3_out, or_4_out, or_5_out, STEP_out, xnor_1_out,
       xnor_2_out, xor_1_out, xor_2_out;
  wire [3:0] com_alu_1_zero_flag;
  wire [7:0] A_REGISTER_data_out, B_REGISTER_data_out, com_alu_1_result, controlled_buffer_1_out,
       controlled_buffer_5_out, FLAG_REGISTER_data_out, INSTRUCTION_REGISTER_data_out,
       MEMADDR_REGISTER_data_out, OUTPUT_A_data_out, OUTPUT_B_data_out, OUTPUT_C_data_out, OUTPUT_D_data_out,
       PROGRAM_COUNTER_data_out, ram_1_dout, rom_1_data, rom_2_data, rom_3_data, rom_4_data, rom_5_data,
       STEP_COUNTER_data_out;

  or or_1 (or_1_out, in_1, rom_2_data[0]);
  LED led_1 (.in(controlled_buffer_1_out[7]));
  LED led_2 (.in(controlled_buffer_1_out[6]));
  LED led_3 (.in(controlled_buffer_1_out[5]));
  Button STEP (.out(STEP_out));
  LED S01_PCR (.in(rom_5_data[7]));
  LED S02_PCW (.in(and_3_out));
  LED S03_PCI (.in(rom_5_data[5]));
  LED S04_MAW (.in(rom_5_data[4]));
  LED S05_IRW (.in(rom_5_data[3]));
  LED S06_MMR (.in(rom_5_data[2]));
  LED S07_MMW (.in(rom_5_data[1]));
  LED S08_ARR (.in(rom_5_data[0]));
  LED S09_ARW (.in(rom_4_data[7]));
  LED S10_BRR (.in(rom_4_data[6]));
  LED S11_BRW (.in(rom_4_data[5]));
  LED S12_ADD (.in(rom_4_data[4]));
  LED S13_SUB (.in(rom_4_data[3]));
  LED S14_NEG (.in(rom_4_data[2]));
  LED S15_AND (.in(rom_4_data[1]));
  LED S16_OR (.in(rom_4_data[0]));
  LED S17_XOR (.in(rom_3_data[7]));
  LED S18_NOT (.in(rom_3_data[6]));
  LED S19_SHL (.in(rom_3_data[5]));
  LED S20_SHR (.in(rom_3_data[4]));
  LED S21_OAW (.in(rom_3_data[3]));
  LED S22_OBW (.in(rom_3_data[2]));
  LED S23_OCW (.in(rom_3_data[1]));
  LED S24_ODW (.in(rom_3_data[0]));
  LED RSC (.in(rom_2_data[1]));
  LED led_4 (.in(controlled_buffer_1_out[4]));
  LED led_5 (.in(controlled_buffer_1_out[3]));
  LED led_6 (.in(controlled_buffer_1_out[2]));
  LED led_7 (.in(controlled_buffer_1_out[1]));
  LED led_8 (.in(controlled_buffer_1_out[0]));
  COM_CLK com_clk_1 (.HALT(or_1_out), .STEP(STEP_out), .CLK(com_clk_1_clk));
  LED led_9 (.in(PROGRAM_COUNTER_data_out[7]));
  LED led_10 (.in(PROGRAM_COUNTER_data_out[6]));
  LED led_11 (.in(A_REGISTER_data_out[7]));
  LED led_12 (.in(B_REGISTER_data_out[7]));
  LED led_13 (.in(PROGRAM_COUNTER_data_out[5]));
  LED led_14 (.in(PROGRAM_COUNTER_data_out[4]));
  LED led_15 (.in(PROGRAM_COUNTER_data_out[3]));
  LED led_16 (.in(PROGRAM_COUNTER_data_out[2]));
  LED led_17 (.in(A_REGISTER_data_out[6]));
  LED led_18 (.in(A_REGISTER_data_out[5]));
  LED led_19 (.in(A_REGISTER_data_out[4]));
  LED led_20 (.in(A_REGISTER_data_out[3]));
  LED led_21 (.in(B_REGISTER_data_out[6]));
  LED led_22 (.in(B_REGISTER_data_out[5]));
  LED led_23 (.in(B_REGISTER_data_out[4]));
  LED led_24 (.in(B_REGISTER_data_out[3]));
  LED led_25 (.in(PROGRAM_COUNTER_data_out[1]));
  LED led_26 (.in(PROGRAM_COUNTER_data_out[0]));
  COM_CNT PROGRAM_COUNTER (
    .READ(1'b1), .WRITE(and_3_out), .INC(rom_5_data[5]), .RESET(RST), .CLK(com_clk_1_clk),
    .DATA_IN(controlled_buffer_1_out), .DATA_OUT(PROGRAM_COUNTER_data_out));  // open: CARRY
  assign controlled_buffer_1_out = rom_5_data[7] ? PROGRAM_COUNTER_data_out : 8'bz;  // Controlled_Buffer controlled_buffer_1
  LED led_27 (.in(A_REGISTER_data_out[2]));
  LED led_28 (.in(A_REGISTER_data_out[1]));
  LED led_29 (.in(A_REGISTER_data_out[0]));
  COM_REG A_REGISTER (
    .DATA_IN(controlled_buffer_1_out), .READ(1'b1), .WRITE(rom_4_data[7]), .RESET(RST), .CLK(com_clk_1_clk),
    .DATA_OUT(A_REGISTER_data_out));
  LED led_30 (.in(B_REGISTER_data_out[2]));
  LED led_31 (.in(B_REGISTER_data_out[1]));
  LED led_32 (.in(B_REGISTER_data_out[0]));
  COM_REG B_REGISTER (
    .DATA_IN(controlled_buffer_1_out), .READ(1'b1), .WRITE(rom_4_data[5]), .RESET(RST), .CLK(com_clk_1_clk),
    .DATA_OUT(B_REGISTER_data_out));
  assign controlled_buffer_1_out = rom_5_data[0] ? A_REGISTER_data_out : 8'bz;  // Controlled_Buffer controlled_buffer_2
  assign controlled_buffer_1_out = rom_4_data[6] ? B_REGISTER_data_out : 8'bz;  // Controlled_Buffer controlled_buffer_3
  LED led_33 (.in(MEMADDR_REGISTER_data_out[7]));
  LED led_34 (.in(MEMADDR_REGISTER_data_out[6]));
  LED led_35 (.in(MEMADDR_REGISTER_data_out[3]));
  LED led_36 (.in(MEMADDR_REGISTER_data_out[2]));
  LED led_37 (.in(MEMADDR_REGISTER_data_out[5]));
  LED led_38 (.in(MEMADDR_REGISTER_data_out[4]));
  LED led_39 (.in(MEMADDR_REGISTER_data_out[1]));
  LED led_40 (.in(MEMADDR_REGISTER_data_out[0]));
  COM_REG MEMADDR_REGISTER (
    .DATA_IN(controlled_buffer_1_out), .READ(1'b1), .WRITE(rom_5_data[4]), .RESET(RST), .CLK(com_clk_1_clk),
    .DATA_OUT(MEMADDR_REGISTER_data_out));
  or or_2 (or_2_out, rom_4_data[4], rom_4_data[3], rom_4_data[1], rom_4_data[0], rom_3_data[7], rom_3_data[6], rom_3_data[5], rom_3_data[4]);
  ROM #(.addrWidth(7)) rom_1 (.addr(MEMADDR_REGISTER_data_out[6:0]), .data(rom_1_data));
  RAM #(.addrWidth(7)) ram_1 (
    .addr(MEMADDR_REGISTER_data_out[6:0]), .we(rom_5_data[1]), .oe(rom_5_data[2]), .clk(com_clk_1_clk),
    .din(controlled_buffer_1_out), .dout(ram_1_dout));
  assign controlled_buffer_1_out = or_2_out ? com_alu_1_result : 8'bz;  // Controlled_Buffer controlled_buffer_4
  COM_ALU com_alu_1 (
    .OP_SUB(rom_4_data[3]), .OP_AND(rom_4_data[1]), .OP_OR(rom_4_data[0]), .OP_XOR(rom_3_data[7]),
    .OP_NOT(rom_3_data[6]), .OP_SHL(rom_3_data[5]), .OP_SHR(rom_3_data[4]), .INPUT_A(A_REGISTER_data_out),
    .INPUT_B(B_REGISTER_data_out), .OP_ADD(rom_4_data[4]), .CARRY_FLAG(com_alu_1_zero_flag[3]),
    .OFLOW_FLAG(com_alu_1_zero_flag[2]), .SIGN_FLAG(com_alu_1_zero_flag[1]), .RESULT(com_alu_1_result),
    .ZERO_FLAG(com_alu_1_zero_flag[0]));  // open: CARRY
  LED led_41 (.in(rom_1_data[7]));
  LED led_42 (.in(rom_1_data[6]));
  LED led_43 (.in(rom_1_data[5]));
  LED led_44 (.in(ram_1_dout[7]));
  LED led_45 (.in(ram_1_dout[6]));
  LED led_46 (.in(ram_1_dout[5]));
  LED led_47 (.in(rom_1_data[4]));
  LED led_48 (.in(rom_1_data[3]));
  LED led_49 (.in(rom_1_data[2]));
  LED led_50 (.in(rom_1_data[1]));
  LED led_51 (.in(ram_1_dout[4]));
  LED led_52 (.in(ram_1_dout[3]));
  LED led_53 (.in(ram_1_dout[2]));
  LED led_54 (.in(ram_1_dout[1]));
  assign controlled_buffer_5_out = or_2_out ? {4'b0000, com_alu_1_zero_flag} : 8'bz;  // Controlled_Buffer controlled_buffer_5
  LED led_55 (.in(rom_1_data[0]));
  LED led_56 (.in(ram_1_dout[0]));
  and and_1 (and_1_out, ~MEMADDR_REGISTER_data_out[7], rom_5_data[2]);  // AND_Gate
  assign controlled_buffer_1_out = and_1_out ? rom_1_data : 8'bz;  // Controlled_Buffer controlled_buffer_6
  and and_2 (and_2_out, MEMADDR_REGISTER_data_out[7], rom_5_data[2]);
  assign controlled_buffer_1_out = and_2_out ? ram_1_dout : 8'bz;  // Controlled_Buffer controlled_buffer_7
  LED led_57 (.in(FLAG_REGISTER_data_out[7]));
  LED led_58 (.in(FLAG_REGISTER_data_out[6]));
  LED led_59 (.in(FLAG_REGISTER_data_out[5]));
  LED led_60 (.in(FLAG_REGISTER_data_out[4]));
  LED led_61 (.in(FLAG_REGISTER_data_out[3]));
  LED led_62 (.in(FLAG_REGISTER_data_out[2]));
  LED led_63 (.in(FLAG_REGISTER_data_out[1]));
  LED led_64 (.in(FLAG_REGISTER_data_out[0]));
  or or_3 (or_3_out, RST, rom_2_data[1], STEP_COUNTER_data_out[4]);
  COM_REG FLAG_REGISTER (
    .DATA_IN(controlled_buffer_5_out), .READ(1'b1), .WRITE(or_2_out), .RESET(RST), .CLK(com_clk_1_clk),
    .DATA_OUT(FLAG_REGISTER_data_out));
  LED led_65 (.in(STEP_COUNTER_data_out[7]));
  LED led_66 (.in(INSTRUCTION_REGISTER_data_out[7]));
  LED led_67 (.in(STEP_COUNTER_data_out[6]));
  LED led_68 (.in(STEP_COUNTER_data_out[5]));
  LED led_69 (.in(STEP_COUNTER_data_out[4]));
  LED led_70 (.in(STEP_COUNTER_data_out[3]));
  LED led_71 (.in(INSTRUCTION_REGISTER_data_out[6]));
  LED led_72 (.in(INSTRUCTION_REGISTER_data_out[5]));
  LED led_73 (.in(INSTRUCTION_REGISTER_data_out[4]));
  LED led_74 (.in(INSTRUCTION_REGISTER_data_out[3]));
  LED led_75 (.in(OUTPUT_A_data_out[7]));
  LED led_76 (.in(OUTPUT_B_data_out[7]));
  LED led_77 (.in(STEP_COUNTER_data_out[2]));
  LED led_78 (.in(STEP_COUNTER_data_out[1]));
  LED led_79 (.in(STEP_COUNTER_data_out[0]));
  COM_CNT STEP_COUNTER (
    .READ(1'b1), .INC(1'b1), .RESET(or_3_out), .CLK(com_clk_1_clk), .DATA_OUT(STEP_COUNTER_data_out));  // open: WRITE, DATA_IN, CARRY
  LED led_80 (.in(INSTRUCTION_REGISTER_data_out[2]));
  LED led_81 (.in(INSTRUCTION_REGISTER_data_out[1]));
  LED led_82 (.in(INSTRUCTION_REGISTER_data_out[0]));
  COM_REG INSTRUCTION_REGISTER (
    .DATA_IN(controlled_buffer_1_out), .READ(1'b1), .WRITE(rom_5_data[3]), .RESET(RST), .CLK(com_clk_1_clk),
    .DATA_OUT(INSTRUCTION_REGISTER_data_out));
  LED led_83 (.in(OUTPUT_A_data_out[6]));
  LED led_84 (.in(OUTPUT_A_data_out[5]));
  LED led_85 (.in(OUTPUT_A_data_out[4]));
  LED led_86 (.in(OUTPUT_A_data_out[3]));
  LED led_87 (.in(OUTPUT_B_data_out[6]));
  LED led_88 (.in(OUTPUT_B_data_out[5]));
  LED led_89 (.in(OUTPUT_B_data_out[4]));
  LED led_90 (.in(OUTPUT_B_data_out[3]));
  LED led_91 (.in(OUTPUT_A_data_out[2]));
  LED led_92 (.in(OUTPUT_A_data_out[1]));
  LED led_93 (.in(OUTPUT_A_data_out[0]));
  COM_REG OUTPUT_A (
    .DATA_IN(controlled_buffer_1_out), .READ(1'b1), .WRITE(rom_3_data[3]), .RESET(RST), .CLK(com_clk_1_clk),
    .DATA_OUT(OUTPUT_A_data_out));
  LED led_94 (.in(OUTPUT_B_data_out[2]));
  LED led_95 (.in(OUTPUT_B_data_out[1]));
  LED led_96 (.in(OUTPUT_B_data_out[0]));
  COM_REG OUTPUT_B (
    .DATA_IN(controlled_buffer_1_out), .READ(1'b1), .WRITE(rom_3_data[2]), .RESET(RST), .CLK(com_clk_1_clk),
    .DATA_OUT(OUTPUT_B_data_out));
  ROM #(.addrWidth(12)) rom_2 (.addr({INSTRUCTION_REGISTER_data_out, STEP_COUNTER_data_out[3:0]}), .data(rom_2_data));
  ROM #(.addrWidth(12)) rom_3 (.addr({INSTRUCTION_REGISTER_data_out, STEP_COUNTER_data_out[3:0]}), .data(rom_3_data));
  ROM #(.addrWidth(12)) rom_4 (.addr({INSTRUCTION_REGISTER_data_out, STEP_COUNTER_data_out[3:0]}), .data(rom_4_data));
  ROM #(.addrWidth(12)) rom_5 (.addr({INSTRUCTION_REGISTER_data_out, STEP_COUNTER_data_out[3:0]}), .data(rom_5_data));
  LED led_97 (.in(rom_2_data[7]));
  LED led_98 (.in(rom_2_data[6]));
  LED led_99 (.in(rom_2_data[5]));
  LED led_100 (.in(rom_3_data[7]));
  LED led_101 (.in(rom_3_data[6]));
  LED led_102 (.in(rom_3_data[5]));
  LED led_103 (.in(rom_4_data[7]));
  LED led_104 (.in(rom_4_data[6]));
  LED led_105 (.in(rom_4_data[5]));
  LED led_106 (.in(rom_5_data[7]));
  LED led_107 (.in(rom_5_data[6]));
  LED led_108 (.in(rom_5_data[5]));
  LED led_109 (.in(OUTPUT_C_data_out[7]));
  LED led_110 (.in(OUTPUT_C_data_out[6]));
  LED led_111 (.in(OUTPUT_C_data_out[5]));
  LED led_112 (.in(OUTPUT_D_data_out[7]));
  LED led_113 (.in(OUTPUT_D_data_out[6]));
  LED led_114 (.in(OUTPUT_D_data_out[5]));
  LED led_115 (.in(rom_2_data[4]));
  LED led_116 (.in(rom_2_data[3]));
  LED led_117 (.in(rom_2_data[2]));
  LED led_118 (.in(rom_2_data[1]));
  LED led_119 (.in(rom_3_data[4]));
  LED led_120 (.in(rom_3_data[3]));
  LED led_121 (.in(rom_3_data[2]));
  LED led_122 (.in(rom_3_data[1]));
  LED led_123 (.in(rom_4_data[4]));
  LED led_124 (.in(rom_4_data[3]));
  LED led_125 (.in(rom_4_data[2]));
  LED led_126 (.in(rom_4_data[1]));
  LED led_127 (.in(rom_5_data[4]));
  LED led_128 (.in(rom_5_data[3]));
  LED led_129 (.in(rom_5_data[2]));
  LED led_130 (.in(rom_5_data[1]));
  LED led_131 (.in(OUTPUT_C_data_out[4]));
  LED led_132 (.in(OUTPUT_C_data_out[3]));
  LED led_133 (.in(OUTPUT_C_data_out[2]));
  LED led_134 (.in(OUTPUT_C_data_out[1]));
  LED led_135 (.in(OUTPUT_D_data_out[4]));
  LED led_136 (.in(OUTPUT_D_data_out[3]));
  LED led_137 (.in(OUTPUT_D_data_out[2]));
  LED led_138 (.in(OUTPUT_D_data_out[1]));
  LED led_139 (.in(rom_2_data[0]));
  LED led_140 (.in(rom_3_data[0]));
  LED led_141 (.in(rom_4_data[0]));
  LED led_142 (.in(rom_5_data[0]));
  LED led_143 (.in(OUTPUT_C_data_out[0]));
  COM_REG OUTPUT_C (
    .DATA_IN(controlled_buffer_1_out), .READ(1'b1), .WRITE(rom_3_data[1]), .RESET(RST), .CLK(com_clk_1_clk),
    .DATA_OUT(OUTPUT_C_data_out));
  LED led_144 (.in(OUTPUT_D_data_out[0]));
  COM_REG OUTPUT_D (
    .DATA_IN(controlled_buffer_1_out), .READ(1'b1), .WRITE(rom_3_data[0]), .RESET(RST), .CLK(com_clk_1_clk),
    .DATA_OUT(OUTPUT_D_data_out));
  or or_4 (or_4_out, and_4_out, and_5_out, and_6_out, and_7_out, and_8_out, and_9_out, and_10_out);
  and and_3 (and_3_out, rom_5_data[6], or_4_out);
  _7_Segment_Display u_7_segment_display_1 (
    .g(OUTPUT_A_data_out[3]), .f(OUTPUT_A_data_out[1]), .a(OUTPUT_A_data_out[0]), .b(OUTPUT_A_data_out[2]),
    .e(OUTPUT_A_data_out[4]), .d(OUTPUT_A_data_out[6]), .c(OUTPUT_A_data_out[5]), .dp(OUTPUT_A_data_out[7]));
  _7_Segment_Display u_7_segment_display_2 (
    .g(OUTPUT_B_data_out[3]), .f(OUTPUT_B_data_out[1]), .a(OUTPUT_B_data_out[0]), .b(OUTPUT_B_data_out[2]),
    .e(OUTPUT_B_data_out[4]), .d(OUTPUT_B_data_out[6]), .c(OUTPUT_B_data_out[5]), .dp(OUTPUT_B_data_out[7]));
  and and_4 (and_4_out, ~rom_2_data[7], ~rom_2_data[6], ~rom_2_data[5], ~rom_2_data[4], ~rom_2_data[3], ~rom_2_data[2]);  // AND_Gate
  and and_5 (and_5_out, rom_2_data[7], FLAG_REGISTER_data_out[0]);
  and and_6 (and_6_out, rom_2_data[6], ~FLAG_REGISTER_data_out[0]);  // AND_Gate
  and and_7 (and_7_out, rom_2_data[5], ~FLAG_REGISTER_data_out[0], xnor_1_out);  // AND_Gate
  xnor xnor_1 (xnor_1_out, FLAG_REGISTER_data_out[1], FLAG_REGISTER_data_out[2]);
  and and_8 (and_8_out, rom_2_data[4], xnor_2_out);
  xnor xnor_2 (xnor_2_out, FLAG_REGISTER_data_out[1], FLAG_REGISTER_data_out[2]);
  and and_9 (and_9_out, rom_2_data[3], xor_1_out);
  and and_10 (and_10_out, rom_2_data[2], or_5_out);
  _7_Segment_Display u_7_segment_display_3 (
    .g(OUTPUT_C_data_out[3]), .f(OUTPUT_C_data_out[1]), .a(OUTPUT_C_data_out[0]), .b(OUTPUT_C_data_out[2]),
    .e(OUTPUT_C_data_out[4]), .d(OUTPUT_C_data_out[6]), .c(OUTPUT_C_data_out[5]), .dp(OUTPUT_C_data_out[7]));
  _7_Segment_Display u_7_segment_display_4 (
    .g(OUTPUT_D_data_out[3]), .f(OUTPUT_D_data_out[1]), .a(OUTPUT_D_data_out[0]), .b(OUTPUT_D_data_out[2]),
    .e(OUTPUT_D_data_out[4]), .d(OUTPUT_D_data_out[6]), .c(OUTPUT_D_data_out[5]), .dp(OUTPUT_D_data_out[7]));
  xor xor_1 (xor_1_out, FLAG_REGISTER_data_out[1], FLAG_REGISTER_data_out[2]);
  or or_5 (or_5_out, FLAG_REGISTER_data_out[0], xor_2_out);
  xor xor_2 (xor_2_out, FLAG_REGISTER_data_out[1], FLAG_REGISTER_data_out[2]);

  // Notes on the sheet:
  //   CENTRAL UNIT
  //   contents of rom_1 (hex, n*v repeats v):
  //   9 6 f 83 9 0 f 80 f 82 f 84 9 1 f 81 a 80 d 81 13 f 82 11 80 d 82 11 81 a 84 c 1 13 f 84 9 0 1d 1e
  //   1f 20 a 82 c 1 16 4 36 9 77 20 2 39 9 24 20 a 82 c 2 16 4 45 9 77 1f 2 48 9 24 1f a 82 c 4 16 4 54 9
  //   77 1e 2 57 9 24 1e a 82 c 8 16 4 63 9 77 1d 2 66 9 24 1d a 84 d 83 1c 4 10 2 4
  //   contents of rom_2 (hex, n*v repeats v):
  //   18*0 1 17*0 2 15*0 80 2 14*0 40 2 14*0 20 2 14*0 10 2 14*0 8 2 14*0 4 2 14*0 2 16*0 2 16*0 2 13*0 2
  //   16*0 2 16*0 2 14*0 2 16*0 2 14*0 2 16*0 2 12*0 2 15*0 2 15*0 2 15*0 2 15*0 2 15*0 2 15*0 2 15*0 2
  //   15*0 2 15*0 2 15*0 2 15*0 2 15*0 2 15*0 2
  //   contents of rom_3 (hex, n*v repeats v):
  //   386*0 80 15*0 40 15*0 20 15*0 10 31*0 8 15*0 4 15*0 2 15*0 1
  //   contents of rom_4 (hex, n*v repeats v):
  //   147*0 80 16*0 80 16*0 80 13*0 20 16*0 20 16*0 20 46*0 40 16*0 40 12*0 90 15*0 88 15*0 84 15*0 82
  //   15*0 81 15*0 80 15*0 80 15*0 80 15*0 80 15*0 8
  //   contents of rom_5 (hex, n*v repeats v):
  //   90 2c 14*0 90 2c 14*0 90 2c 90 44 12*0 90 2c 90 20 44 11*0 90 2c 90 20 44 11*0 90 2c 90 20 44 11*0
  //   90 2c 90 20 44 11*0 90 2c 90 20 44 11*0 90 2c 90 20 44 11*0 90 2c 90 24 12*0 90 2c 90 34 4 11*0 90
  //   2c 90 34 14 4 10*0 90 2c 90 34 12*0 90 2c 90 34 4 11*0 90 2c 90 34 14 4 10*0 90 2c 90 34 3 11*0 90
  //   2c 90 34 14 3 10*0 90 2c 90 34 2 11*0 90 2c 90 34 14 2 10*0 90 2c 14*0 90 2c 14*0 90 2c 14*0 90 2c
  //   14*0 90 2c 14*0 90 2c 14*0 90 2c 14*0 90 2c 14*0 90 2c 14*0 90 2c 14*0 90 2c 1 13*0 90 2c 1 13*0 90
  //   2c 1 13*0 90 2c 1
  //   MICROCODE_BYTE_4
  //   MICROCODE_BYTE_3
  //   MICROCODE_BYTE_2
  //   MICROCODE_BYTE_1
  //   JEQ
  //   JNQ
  //   JGR
  //   JGQ
  //   JLE
  //   JLQ
endmodule

module COM_ALU (
  input  [7:0] INPUT_A,
  input  [7:0] INPUT_B,
  input  CARRY,
  input  OP_ADD,
  input  OP_SUB,
  input  OP_AND,
  input  OP_OR,
  input  OP_XOR,
  input  OP_NOT,
  input  OP_SHL,
  input  OP_SHR,
  output [7:0] RESULT,
  output CARRY_FLAG,
  output OFLOW_FLAG,
  output SIGN_FLAG,
  output ZERO_FLAG
);

  wire and_1_out, and_2_out, and_3_out, and_4_out, and_5_out, and_6_out, and_7_out, and_8_out, and_9_out,
       and_10_out, and_11_out, and_12_out, and_13_out, and_14_out, and_15_out, and_16_out, and_18_out,
       and_20_out, and_21_out, and_22_out, nor_1_out, nor_2_out, nor_3_out, or_1_out, or_2_out, or_3_out,
       or_4_out, or_5_out, or_6_out, or_7_out, or_8_out, or_9_out, or_11_out, or_12_out, or_13_out,
       or_14_out, or_15_out, or_16_out, xor_2_out, xor_3_out, xor_4_out, xor_5_out, xor_6_out, xor_7_out,
       xor_8_out, xor_9_out;
  wire [7:0] and_17_out, not_1_out, or_10_out, xor_1_out, xor_10_out, xor_18_out;

  assign xor_1_out = INPUT_B ^ {8{OP_SUB}};  // XOR_Gate xor_1, 8 bits wide
  or or_1 (or_1_out, CARRY, OP_SUB);
  xor xor_2 (xor_2_out, INPUT_A[0], xor_1_out[0]);
  and and_1 (and_1_out, INPUT_A[0], xor_1_out[0]);
  xor xor_3 (xor_3_out, INPUT_A[1], xor_1_out[1]);
  and and_2 (and_2_out, INPUT_A[1], xor_1_out[1]);
  xor xor_4 (xor_4_out, INPUT_A[2], xor_1_out[2]);
  and and_3 (and_3_out, INPUT_A[2], xor_1_out[2]);
  xor xor_5 (xor_5_out, INPUT_A[3], xor_1_out[3]);
  and and_4 (and_4_out, INPUT_A[3], xor_1_out[3]);
  xor xor_6 (xor_6_out, INPUT_A[4], xor_1_out[4]);
  and and_5 (and_5_out, INPUT_A[4], xor_1_out[4]);
  xor xor_7 (xor_7_out, INPUT_A[5], xor_1_out[5]);
  and and_6 (and_6_out, INPUT_A[5], xor_1_out[5]);
  xor xor_8 (xor_8_out, INPUT_A[6], xor_1_out[6]);
  and and_7 (and_7_out, INPUT_A[6], xor_1_out[6]);
  xor xor_9 (xor_9_out, INPUT_A[7], xor_1_out[7]);
  and and_8 (and_8_out, INPUT_A[7], xor_1_out[7]);
  xor xor_10 (xor_10_out[0], xor_2_out, or_1_out);
  and and_9 (and_9_out, xor_2_out, or_1_out);
  or or_2 (or_2_out, and_9_out, and_1_out);
  xor xor_11 (xor_10_out[1], xor_3_out, or_2_out);
  and and_10 (and_10_out, xor_3_out, or_2_out);
  or or_3 (or_3_out, and_10_out, and_2_out);
  xor xor_12 (xor_10_out[2], xor_4_out, or_3_out);
  and and_11 (and_11_out, xor_4_out, or_3_out);
  or or_4 (or_4_out, and_11_out, and_3_out);
  xor xor_13 (xor_10_out[3], xor_5_out, or_4_out);
  and and_12 (and_12_out, xor_5_out, or_4_out);
  or or_5 (or_5_out, and_12_out, and_4_out);
  xor xor_14 (xor_10_out[4], xor_6_out, or_5_out);
  and and_13 (and_13_out, xor_6_out, or_5_out);
  or or_6 (or_6_out, and_13_out, and_5_out);
  xor xor_15 (xor_10_out[5], xor_7_out, or_6_out);
  and and_14 (and_14_out, xor_7_out, or_6_out);
  or or_7 (or_7_out, and_14_out, and_6_out);
  xor xor_16 (xor_10_out[6], xor_8_out, or_7_out);
  and and_15 (and_15_out, xor_8_out, or_7_out);
  or or_8 (or_8_out, and_15_out, and_7_out);
  xor xor_17 (xor_10_out[7], xor_9_out, or_8_out);
  and and_16 (and_16_out, xor_9_out, or_8_out);
  or or_9 (or_9_out, and_16_out, and_8_out);
  assign and_17_out = INPUT_A & xor_1_out;  // AND_Gate and_17, 8 bits wide
  assign or_10_out = INPUT_A | xor_1_out;  // OR_Gate or_10, 8 bits wide
  assign xor_18_out = INPUT_A ^ xor_1_out;  // XOR_Gate xor_18, 8 bits wide
  assign not_1_out = ~INPUT_A;  // NOT_Gate not_1, 8 bits wide
  assign RESULT = or_11_out ? xor_10_out : 8'bz;  // Controlled_Buffer controlled_buffer_1
  or or_11 (or_11_out, OP_ADD, OP_SUB);
  and and_18 (and_18_out, or_11_out, or_9_out);
  and and_19 (OFLOW_FLAG, or_11_out, or_12_out);
  nor nor_1 (nor_1_out, INPUT_A[7], xor_1_out[7]);
  and and_20 (and_20_out, INPUT_A[7], xor_1_out[7]);
  xor xor_19 (CARRY_FLAG, OP_SUB, and_18_out);
  or or_12 (or_12_out, and_21_out, and_22_out);
  and and_21 (and_21_out, nor_1_out, xor_10_out[7]);
  and and_22 (and_22_out, and_20_out, ~xor_10_out[7]);  // AND_Gate
  assign RESULT = OP_AND ? and_17_out : 8'bz;  // Controlled_Buffer controlled_buffer_2
  assign RESULT = OP_OR ? or_10_out : 8'bz;  // Controlled_Buffer controlled_buffer_3
  assign RESULT = OP_XOR ? xor_18_out : 8'bz;  // Controlled_Buffer controlled_buffer_4
  assign RESULT = OP_NOT ? not_1_out : 8'bz;  // Controlled_Buffer controlled_buffer_5
  assign RESULT = OP_SHL ? {INPUT_A[6:0], 1'b0} : 8'bz;  // Controlled_Buffer controlled_buffer_6
  assign RESULT = OP_SHR ? {1'b0, INPUT_A[7:1]} : 8'bz;  // Controlled_Buffer controlled_buffer_7
  or or_13 (or_13_out, RESULT[7], RESULT[6]);
  or or_14 (or_14_out, RESULT[5], RESULT[4]);
  nor nor_2 (nor_2_out, or_13_out, or_14_out);
  or or_15 (or_15_out, RESULT[3], RESULT[2]);
  or or_16 (or_16_out, RESULT[1], RESULT[0]);
  nor nor_3 (nor_3_out, or_15_out, or_16_out);
  and and_23 (ZERO_FLAG, nor_2_out, nor_3_out);

  assign SIGN_FLAG = RESULT[7];

  // Notes on the sheet:
  //   ALU
endmodule

module COM_CLK (
  input  HALT,
  input  STEP,
  output CLK
);

  wire and_1_out, clock_1_out, not_1_out, or_1_out;

  Clock clock_1 (.out(clock_1_out));
  not not_1 (not_1_out, HALT);
  or or_1 (or_1_out, not_1_out, STEP);
  and and_1 (and_1_out, clock_1_out, or_1_out);
  or or_2 (CLK, and_1_out, STEP);

  // Notes on the sheet:
  //   CLOCK
endmodule

module COM_REG (
  input  [7:0] DATA_IN,
  input  READ,
  input  WRITE,
  input  RESET,
  input  CLK,
  output [7:0] DATA_OUT
);

  wire and_1_out, and_2_out, and_3_out, and_4_out, and_5_out, and_6_out, and_7_out, and_8_out, and_9_out,
       and_10_out, and_11_out, and_12_out, and_13_out, and_14_out, and_15_out, and_16_out, d_ff_1_q,
       d_ff_2_q, d_ff_3_q, d_ff_4_q, d_ff_5_q, d_ff_6_q, d_ff_7_q, d_ff_8_q, or_1_out, or_2_out, or_3_out,
       or_4_out, or_5_out, or_6_out, or_7_out, or_8_out;

  and and_1 (and_1_out, WRITE, DATA_IN[0]);
  and and_2 (and_2_out, ~WRITE, d_ff_1_q);  // AND_Gate
  or or_1 (or_1_out, and_1_out, and_2_out);
  D_Flip_Flop #(.trigger("falling")) d_ff_1 (.D(or_1_out), .clk(CLK), .Q(d_ff_1_q), .reset(RESET));  // open: Qn, preset
  assign DATA_OUT[0] = READ ? d_ff_1_q : 1'bz;  // Controlled_Buffer controlled_buffer_1
  and and_3 (and_3_out, WRITE, DATA_IN[1]);
  or or_2 (or_2_out, and_3_out, and_4_out);
  D_Flip_Flop #(.trigger("falling")) d_ff_2 (.D(or_2_out), .clk(CLK), .Q(d_ff_2_q), .reset(RESET));  // open: Qn, preset
  assign DATA_OUT[1] = READ ? d_ff_2_q : 1'bz;  // Controlled_Buffer controlled_buffer_2
  and and_4 (and_4_out, ~WRITE, d_ff_2_q);  // AND_Gate
  and and_5 (and_5_out, WRITE, DATA_IN[2]);
  assign DATA_OUT[2] = READ ? d_ff_3_q : 1'bz;  // Controlled_Buffer controlled_buffer_3
  and and_6 (and_6_out, ~WRITE, d_ff_3_q);  // AND_Gate
  or or_3 (or_3_out, and_5_out, and_6_out);
  D_Flip_Flop #(.trigger("falling")) d_ff_3 (.D(or_3_out), .clk(CLK), .Q(d_ff_3_q), .reset(RESET));  // open: Qn, preset
  and and_7 (and_7_out, WRITE, DATA_IN[3]);
  and and_8 (and_8_out, ~WRITE, d_ff_4_q);  // AND_Gate
  or or_4 (or_4_out, and_7_out, and_8_out);
  D_Flip_Flop #(.trigger("falling")) d_ff_4 (.D(or_4_out), .clk(CLK), .Q(d_ff_4_q), .reset(RESET));  // open: Qn, preset
  assign DATA_OUT[3] = READ ? d_ff_4_q : 1'bz;  // Controlled_Buffer controlled_buffer_4
  and and_9 (and_9_out, WRITE, DATA_IN[4]);
  and and_10 (and_10_out, ~WRITE, d_ff_5_q);  // AND_Gate
  or or_5 (or_5_out, and_9_out, and_10_out);
  D_Flip_Flop #(.trigger("falling")) d_ff_5 (.D(or_5_out), .clk(CLK), .Q(d_ff_5_q), .reset(RESET));  // open: Qn, preset
  assign DATA_OUT[4] = READ ? d_ff_5_q : 1'bz;  // Controlled_Buffer controlled_buffer_5
  and and_11 (and_11_out, WRITE, DATA_IN[5]);
  or or_6 (or_6_out, and_11_out, and_12_out);
  D_Flip_Flop #(.trigger("falling")) d_ff_6 (.D(or_6_out), .clk(CLK), .Q(d_ff_6_q), .reset(RESET));  // open: Qn, preset
  assign DATA_OUT[5] = READ ? d_ff_6_q : 1'bz;  // Controlled_Buffer controlled_buffer_6
  and and_12 (and_12_out, ~WRITE, d_ff_6_q);  // AND_Gate
  and and_13 (and_13_out, WRITE, DATA_IN[6]);
  assign DATA_OUT[6] = READ ? d_ff_7_q : 1'bz;  // Controlled_Buffer controlled_buffer_7
  and and_14 (and_14_out, ~WRITE, d_ff_7_q);  // AND_Gate
  or or_7 (or_7_out, and_13_out, and_14_out);
  D_Flip_Flop #(.trigger("falling")) d_ff_7 (.D(or_7_out), .clk(CLK), .Q(d_ff_7_q), .reset(RESET));  // open: Qn, preset
  and and_15 (and_15_out, WRITE, DATA_IN[7]);
  and and_16 (and_16_out, ~WRITE, d_ff_8_q);  // AND_Gate
  or or_8 (or_8_out, and_15_out, and_16_out);
  D_Flip_Flop #(.trigger("falling")) d_ff_8 (.D(or_8_out), .clk(CLK), .Q(d_ff_8_q), .reset(RESET));  // open: Qn, preset
  assign DATA_OUT[7] = READ ? d_ff_8_q : 1'bz;  // Controlled_Buffer controlled_buffer_8

  // Notes on the sheet:
  //   REGISTER
endmodule

module COM_CNT (
  input  [7:0] DATA_IN,
  input  READ,
  input  WRITE,
  input  INC,
  input  RESET,
  input  CLK,
  output [7:0] DATA_OUT,
  output CARRY
);

  wire and_1_out, and_2_out, and_3_out, and_4_out, and_5_out, and_6_out, and_7_out, and_8_out, and_9_out,
       and_10_out, and_11_out, and_12_out, and_13_out, and_14_out, and_15_out, and_16_out, and_17_out,
       and_18_out, and_19_out, and_20_out, and_21_out, and_22_out, and_23_out, and_24_out, and_25_out,
       and_26_out, and_27_out, and_28_out, and_29_out, and_30_out, j_k_ff_1_q, j_k_ff_2_q, j_k_ff_3_q,
       j_k_ff_4_q, j_k_ff_5_q, j_k_ff_6_q, j_k_ff_7_q, j_k_ff_8_q, or_1_out, or_2_out, or_3_out, or_4_out,
       or_5_out, or_6_out, or_7_out, or_8_out, or_9_out, or_10_out, or_11_out, or_12_out, or_13_out,
       or_14_out, or_15_out, or_16_out;

  and and_1 (and_1_out, ~DATA_IN[0], WRITE);  // AND_Gate
  or or_1 (or_1_out, INC, and_1_out);
  or or_2 (or_2_out, INC, and_2_out);
  assign DATA_OUT[0] = READ ? j_k_ff_1_q : 1'bz;  // Controlled_Buffer controlled_buffer_1
  and and_2 (and_2_out, DATA_IN[0], WRITE);
  J_K_Flip_Flop #(.trigger("falling")) j_k_ff_1 (
    .J(or_2_out), .K(or_1_out), .clk(CLK), .Q(j_k_ff_1_q), .reset(RESET));  // open: Qn, preset
  and and_3 (and_3_out, ~DATA_IN[1], WRITE);  // AND_Gate
  and and_4 (and_4_out, INC, j_k_ff_1_q);
  or or_3 (or_3_out, and_4_out, and_3_out);
  and and_5 (and_5_out, DATA_IN[1], WRITE);
  or or_4 (or_4_out, and_4_out, and_5_out);
  J_K_Flip_Flop #(.trigger("falling")) j_k_ff_2 (
    .J(or_4_out), .K(or_3_out), .clk(CLK), .Q(j_k_ff_2_q), .reset(RESET));  // open: Qn, preset
  assign DATA_OUT[1] = READ ? j_k_ff_2_q : 1'bz;  // Controlled_Buffer controlled_buffer_2
  and and_6 (and_6_out, INC, and_7_out);
  and and_7 (and_7_out, j_k_ff_2_q, j_k_ff_1_q);
  and and_8 (and_8_out, ~DATA_IN[2], WRITE);  // AND_Gate
  and and_9 (and_9_out, DATA_IN[2], WRITE);
  or or_5 (or_5_out, and_6_out, and_8_out);
  or or_6 (or_6_out, and_6_out, and_9_out);
  J_K_Flip_Flop #(.trigger("falling")) j_k_ff_3 (
    .J(or_6_out), .K(or_5_out), .clk(CLK), .Q(j_k_ff_3_q), .reset(RESET));  // open: Qn, preset
  assign DATA_OUT[2] = READ ? j_k_ff_3_q : 1'bz;  // Controlled_Buffer controlled_buffer_3
  and and_10 (and_10_out, j_k_ff_3_q, and_7_out);
  and and_11 (and_11_out, ~DATA_IN[3], WRITE);  // AND_Gate
  and and_12 (and_12_out, INC, and_10_out);
  or or_7 (or_7_out, and_12_out, and_11_out);
  assign DATA_OUT[3] = READ ? j_k_ff_4_q : 1'bz;  // Controlled_Buffer controlled_buffer_4
  and and_13 (and_13_out, DATA_IN[3], WRITE);
  or or_8 (or_8_out, and_12_out, and_13_out);
  J_K_Flip_Flop #(.trigger("falling")) j_k_ff_4 (
    .J(or_8_out), .K(or_7_out), .clk(CLK), .Q(j_k_ff_4_q), .reset(RESET));  // open: Qn, preset
  and and_14 (and_14_out, INC, and_15_out);
  and and_15 (and_15_out, j_k_ff_4_q, and_10_out);
  or or_9 (or_9_out, and_14_out, and_17_out);
  and and_16 (and_16_out, DATA_IN[4], WRITE);
  and and_17 (and_17_out, ~DATA_IN[4], WRITE);  // AND_Gate
  or or_10 (or_10_out, and_14_out, and_16_out);
  J_K_Flip_Flop #(.trigger("falling")) j_k_ff_5 (
    .J(or_10_out), .K(or_9_out), .clk(CLK), .Q(j_k_ff_5_q), .reset(RESET));  // open: Qn, preset
  assign DATA_OUT[4] = READ ? j_k_ff_5_q : 1'bz;  // Controlled_Buffer controlled_buffer_5
  and and_18 (and_18_out, j_k_ff_5_q, and_15_out);
  and and_19 (and_19_out, ~DATA_IN[5], WRITE);  // AND_Gate
  and and_20 (and_20_out, DATA_IN[5], WRITE);
  and and_21 (and_21_out, INC, and_18_out);
  or or_11 (or_11_out, and_21_out, and_19_out);
  or or_12 (or_12_out, and_21_out, and_20_out);
  assign DATA_OUT[5] = READ ? j_k_ff_6_q : 1'bz;  // Controlled_Buffer controlled_buffer_6
  and and_22 (and_22_out, j_k_ff_6_q, and_18_out);
  J_K_Flip_Flop #(.trigger("falling")) j_k_ff_6 (
    .J(or_12_out), .K(or_11_out), .clk(CLK), .Q(j_k_ff_6_q), .reset(RESET));  // open: Qn, preset
  and and_23 (and_23_out, ~DATA_IN[6], WRITE);  // AND_Gate
  and and_24 (and_24_out, INC, and_22_out);
  or or_13 (or_13_out, and_24_out, and_23_out);
  and and_25 (and_25_out, DATA_IN[6], WRITE);
  or or_14 (or_14_out, and_24_out, and_25_out);
  J_K_Flip_Flop #(.trigger("falling")) j_k_ff_7 (
    .J(or_14_out), .K(or_13_out), .clk(CLK), .Q(j_k_ff_7_q), .reset(RESET));  // open: Qn, preset
  assign DATA_OUT[6] = READ ? j_k_ff_7_q : 1'bz;  // Controlled_Buffer controlled_buffer_7
  and and_26 (and_26_out, INC, and_27_out);
  and and_27 (and_27_out, j_k_ff_7_q, and_22_out);
  and and_28 (and_28_out, ~DATA_IN[7], WRITE);  // AND_Gate
  and and_29 (and_29_out, DATA_IN[7], WRITE);
  or or_15 (or_15_out, and_26_out, and_28_out);
  or or_16 (or_16_out, and_26_out, and_29_out);
  J_K_Flip_Flop #(.trigger("falling")) j_k_ff_8 (
    .J(or_16_out), .K(or_15_out), .clk(CLK), .Q(j_k_ff_8_q), .reset(RESET));  // open: Qn, preset
  assign DATA_OUT[7] = READ ? j_k_ff_8_q : 1'bz;  // Controlled_Buffer controlled_buffer_8
  and and_30 (and_30_out, j_k_ff_8_q, and_27_out);
  and and_31 (CARRY, INC, and_30_out);

  // Notes on the sheet:
  //   COUNTER
endmodule
